# Fritzing sketch SketchIrrigacao (saved by Fritzing 0.9.10b)
breadboards: 1

parts:
  Arduino_UNO = Arduino Uno (Rev3)
  R1 = Resistor [tolerance=±5% power=0.25 resistance=220 package=THT]
  LED1 = LED - 3mm [color="Red (633nm)" current=0.030 package="3 mm [THT]"]
  R2 = Resistor [tolerance=±5% power=0.25 resistance=220 package=THT]
  LED2 = LED - 3mm [color="Yellow (595nm)" current=0.030 package="3 mm [THT]"]
  R3 = Resistor [tolerance=±5% power=0.25 resistance=220 package=THT]
  LED3 = LED - 3mm [color="Green (570nm)" current=0.030 package="3 mm [THT]"]
  부품3 = FC-28 Soil Hygrometer Module
  부품4 = FC-28 Soil Hygrometer Module - Probe
  J1 = Piezo Speaker
  R4 = Resistor [tolerance=±5% resistance=220 package="0402 [SMD]"]
  WATER_PUMP1 = water pump/motor  # not connected
  KY-1 = Keyes Relay [package=THT]
  VCC1 = Battery
  NodeMCU_ESP_8266_(ESP-12E)_AMICA = Amica NodeMCU DEVKIT 1.0
  U1 = Voltage Regulator -- 3.3 V -- LM1117

nets:
  N1: Arduino_UNO.D10_PWM/SS, J1.pin2
  N2: Arduino_UNO.D12/MISO, U1.IN
  GND: Arduino_UNO.GND, R1.Pin_0, R2.Pin_0, R3.Pin_0, 부품3.GND, R4.Pin_0, KY-1.ground, U1.GND
  N3: Arduino_UNO.D2, 부품3.DO
  N4: Arduino_UNO.D3_PWM, KY-1.signal
  N5: Arduino_UNO.D5_PWM, LED1.anode
  N6: Arduino_UNO.D6_PWM, LED2.anode
  N7: Arduino_UNO.D7, LED3.anode
  5V: Arduino_UNO.5V, 부품3.VCC, KY-1.power
  N8: R1.Pin_1, LED1.cathode
  N9: R2.Pin_1, LED2.cathode
  N10: R3.Pin_1, LED3.cathode
  N11: 부품3.POS, 부품4.POS, 부품4.NEG
  N12: J1.pin1, R4.Pin_1
  N13: KY-1.C, VCC1.+
  N14: NodeMCU_ESP_8266_(ESP-12E)_AMICA.pin1, NodeMCU_ESP_8266_(ESP-12E)_AMICA.pin_10, NodeMCU_ESP_8266_(ESP-12E)_AMICA.pin_26
  N15: NodeMCU_ESP_8266_(ESP-12E)_AMICA.pin2, NodeMCU_ESP_8266_(ESP-12E)_AMICA.pin_9, NodeMCU_ESP_8266_(ESP-12E)_AMICA.pin_25, NodeMCU_ESP_8266_(ESP-12E)_AMICA.pin_29
  N16: NodeMCU_ESP_8266_(ESP-12E)_AMICA.pin_13, U1.OUT

notes:
  Placa microcontroladora ARDUINO UNO, que controla o sistema de irrigação automática
  Sensor de umidade do solo volumétrico
  Módulo de controle do sensor de umidade do solo (5V)
  "Buzzer" com alerta sonoro para indicação de acionamento do sistema.
  Relé para controle do acionamento da mini-bomba de água submersível
  Fonte de energia da mini-bomba de água submersível
  Mini-bomba de água submersível, cujo acionamento é controlado pelo relé
  LEDs vermelho, amarelo e verde, para indicar o funcionamento do sistema
  Alimentação da placa Arduino UNO por meio de conexão USB com o computador (12 V)
  Placa microcontroladora NodeMCU ESP 8266 (ESP-12E), modelo Amica, que transmite mensagens para a Internet, por meio do protocolo MQTT
  Fio que liga o pino digital 12 do Arduino no pino digital 2 (GPIO4) da placa NodeMCU (vide tabela de pinos abaixo
  Regulador de tensão AMS 1117, com step-down de 5V para 3.3V.

custom parts:
  FC-28 Soil Hygrometer Module: The FC-28 is a soil hygrometer module that uses the Texas Instruments LM393 comparator chip to provide an analog measurement of soil humidity. The digital output is high when soil moisture is over a certain threshold, as determined by adjusting the potentiometer.
  FC-28 Soil Hygrometer Module - Probe: The FC-28 is a soil hygrometer module that uses the Texas Instruments LM393 comparator chip to provide an analog measurement of soil humidity.
  water pump/motor: WATER PUMP BY ARDUBLOCKTR
  Keyes Relay: The Keyes 5V relay module is suitable for SCM development, home appliance control. It uses a 5V~12V TIL control signal which can control DC / AC signal.
  Voltage Regulator -- 3.3 V -- LM1117: LM1117-3.3 Voltage regulator, 3.3 V output. Note that the pinout order is not the same as LM7805 or LM7833.
